// Logisim project bridge-proof.circ as structural Verilog: 1 circuit, main circuit ReplayHarness
module ReplayHarness (
  output [2:0] sample_index,
  output [31:0] sensor_word,
  output [7:0] V,
  output [7:0] T,
  output [7:0] G,
  output [7:0] A,
  output v_above_70,
  output result_valid,
  output [2:0] phase,
  output reset,
  output [2:0] address,
  output [31:0] ram_word,
  output boot_ready,
  output halt
);

  wire ADVANCE, CAPTURE, CLK;

  Clock clock_1 (.out(CLK));
  Register #(.width(1), .trigger("falling")) u_BOOT_READY (.D(1'b1), .en(1'b1), .Q(boot_ready), .clk(CLK), .clr(1'b0));
  Counter #(.width(3), .max('h7), .ongoal("wrap")) u_PHASE (
    .load(1'b0), .D(3'b000), .count(1'b1), .Q(phase), .up(1'b1), .clk(CLK), .clr(reset));  // open: carry
  Counter #(.width(3), .max('h7), .ongoal("wrap")) u_ADDRESS (
    .load(1'b0), .D(3'b000), .count(ADVANCE), .Q(address), .up(1'b1), .clk(CLK), .clr(reset));  // open: carry
  not not_1 (reset, boot_ready);
  Comparator #(.width(3), .mode("unsigned")) PHASE_2_CAPTURE (.a(phase), .b(3'b010), .eq(CAPTURE));  // open: gt, lt
  Comparator #(.width(3), .mode("unsigned")) PHASE_3_PUBLISH (
    .a(phase), .b(3'b011), .eq(result_valid));  // open: gt, lt
  Comparator #(.width(3), .mode("unsigned")) PHASE_7_ADVANCE (.a(phase), .b(3'b111), .eq(ADVANCE));  // open: gt, lt
  Comparator #(.width(3), .mode("unsigned")) ADDRESS_4_HALT (.a(address), .b(3'b100), .eq(halt));  // open: gt, lt
  RAM #(.addrWidth(3), .dataWidth(32), .enables("byte"), .databus("bibus"), .asyncread("true"), .clearpin("false")) STIMULUS_READ_ONLY (
    .addr(address), .we(1'b0), .oe(1'b1), .clk(1'b0), .din({32{1'b0}}), .dout(ram_word));
  Register #(.width(32)) SNAPSHOT_WORD (
    .D(ram_word), .en(CAPTURE), .Q({A, G, sensor_word[15:0]}), .clk(CLK), .clr(reset));
  Register #(.width(3)) SNAPSHOT_INDEX (.D(address), .en(CAPTURE), .Q(sample_index), .clk(CLK), .clr(reset));
  Comparator #(.width(8), .mode("unsigned")) V_GT_70 (
    .a(sensor_word[7:0]), .b(8'h46), .gt(v_above_70));  // open: eq, lt

  assign sensor_word[31:16] = {A, G};
  assign T = sensor_word[15:8];
  assign V = sensor_word[7:0];

  // Other names for the same wires on the sheet: PUBLISH = result_valid; SNAPSHOT_INDEX[2:0] = sample_index;
  //   SNAPSHOT_WORD[31:0] = {A, G, sensor_word[15:0]}; V_GT_70 = v_above_70
endmodule
