// Logisim project volcano-demo.circ as structural Verilog: 3 circuits, main circuit MonitorGUI
module WindowCounters (
  input  clk,
  input  reset,
  input  sample_enable,
  input  [3:0] flags,
  input  [2:0] k,
  input  fault,
  output [31:0] current_counts,
  output [31:0] last_completed,
  output [31:0] window_meta
);

  wire AND_3, eq_2, gt_10;
  wire [3:0] AND_18, AND_19, AND_28, AND_29, AND_38, AND_39, AND_48, AND_49, AND_68, AND_69, AND_78, AND_79,
       AND_87, AND_88, NOT_17, NOT_27, NOT_37, NOT_47, NOT_67, NOT_77, NOT_86, OR_20, OR_30, OR_40, OR_50,
       OR_70, OR_80, OR_89, sum_13, sum_23, sum_33, sum_43, sum_63, sum_73, sum_82;
  wire [5:0] AND_58, AND_59, NOT_57, OR_60, sum_53, sum_91;

  Comparator #(.width(4), .mode("unsigned")) comparator_1 (
    .a(window_meta[3:0]), .b(4'b1001), .eq(eq_2));  // open: gt, lt
  and and_1 (AND_3, eq_2, sample_enable);
  Comparator #(.width(3), .mode("unsigned")) comparator_2 (.a(k), .b(3'b000), .gt(gt_10));  // open: eq, lt
  Adder #(.width(4)) adder_1 (.a(current_counts[3:0]), .b({3'b000, flags[0]}), .out(sum_13), .cin(1'b0));  // open: cout
  assign NOT_17 = ~{4{eq_2}};  // NOT_Gate not_1, 4 bits wide
  assign AND_18 = NOT_17 & sum_13;  // AND_Gate and_2, 4 bits wide
  assign AND_19 = {4{eq_2}} & 4'b0000;  // AND_Gate and_3, 4 bits wide
  assign OR_20 = AND_18 | AND_19;  // OR_Gate or_1, 4 bits wide
  Register #(.width(4), .trigger("rising")) CURRENT_V (
    .D(OR_20), .en(sample_enable), .Q(current_counts[3:0]), .clk(clk), .clr(reset));
  Register #(.width(4), .trigger("rising")) COMPLETED_V (
    .D(sum_13), .en(AND_3), .Q(last_completed[3:0]), .clk(clk), .clr(reset));
  Adder #(.width(4)) adder_2 (.a(current_counts[7:4]), .b({3'b000, flags[1]}), .out(sum_23), .cin(1'b0));  // open: cout
  assign NOT_27 = ~{4{eq_2}};  // NOT_Gate not_2, 4 bits wide
  assign AND_28 = NOT_27 & sum_23;  // AND_Gate and_4, 4 bits wide
  assign AND_29 = {4{eq_2}} & 4'b0000;  // AND_Gate and_5, 4 bits wide
  assign OR_30 = AND_28 | AND_29;  // OR_Gate or_2, 4 bits wide
  Register #(.width(4), .trigger("rising")) CURRENT_T (
    .D(OR_30), .en(sample_enable), .Q(current_counts[7:4]), .clk(clk), .clr(reset));
  Register #(.width(4), .trigger("rising")) COMPLETED_T (
    .D(sum_23), .en(AND_3), .Q(last_completed[7:4]), .clk(clk), .clr(reset));
  Adder #(.width(4)) adder_3 (
    .a(current_counts[11:8]), .b({3'b000, flags[2]}), .out(sum_33), .cin(1'b0));  // open: cout
  assign NOT_37 = ~{4{eq_2}};  // NOT_Gate not_3, 4 bits wide
  assign AND_38 = NOT_37 & sum_33;  // AND_Gate and_6, 4 bits wide
  assign AND_39 = {4{eq_2}} & 4'b0000;  // AND_Gate and_7, 4 bits wide
  assign OR_40 = AND_38 | AND_39;  // OR_Gate or_3, 4 bits wide
  Register #(.width(4), .trigger("rising")) CURRENT_G (
    .D(OR_40), .en(sample_enable), .Q(current_counts[11:8]), .clk(clk), .clr(reset));
  Register #(.width(4), .trigger("rising")) COMPLETED_G (
    .D(sum_33), .en(AND_3), .Q(last_completed[11:8]), .clk(clk), .clr(reset));
  Adder #(.width(4)) adder_4 (
    .a(current_counts[15:12]), .b({3'b000, flags[3]}), .out(sum_43), .cin(1'b0));  // open: cout
  assign NOT_47 = ~{4{eq_2}};  // NOT_Gate not_4, 4 bits wide
  assign AND_48 = NOT_47 & sum_43;  // AND_Gate and_8, 4 bits wide
  assign AND_49 = {4{eq_2}} & 4'b0000;  // AND_Gate and_9, 4 bits wide
  assign OR_50 = AND_48 | AND_49;  // OR_Gate or_4, 4 bits wide
  Register #(.width(4), .trigger("rising")) CURRENT_A (
    .D(OR_50), .en(sample_enable), .Q(current_counts[15:12]), .clk(clk), .clr(reset));
  Register #(.width(4), .trigger("rising")) COMPLETED_A (
    .D(sum_43), .en(AND_3), .Q(last_completed[15:12]), .clk(clk), .clr(reset));
  Adder #(.width(6)) adder_5 (.a(current_counts[21:16]), .b({3'b000, k}), .out(sum_53), .cin(1'b0));  // open: cout
  assign NOT_57 = ~{6{eq_2}};  // NOT_Gate not_5, 6 bits wide
  assign AND_58 = NOT_57 & sum_53;  // AND_Gate and_10, 6 bits wide
  assign AND_59 = {6{eq_2}} & {6{1'b0}};  // AND_Gate and_11, 6 bits wide
  assign OR_60 = AND_58 | AND_59;  // OR_Gate or_5, 6 bits wide
  Register #(.width(6), .trigger("rising")) CURRENT_readings (
    .D(OR_60), .en(sample_enable), .Q(current_counts[21:16]), .clk(clk), .clr(reset));
  Register #(.width(6), .trigger("rising")) COMPLETED_readings (
    .D(sum_53), .en(AND_3), .Q(last_completed[21:16]), .clk(clk), .clr(reset));
  Adder #(.width(4)) adder_6 (.a(current_counts[25:22]), .b({3'b000, gt_10}), .out(sum_63), .cin(1'b0));  // open: cout
  assign NOT_67 = ~{4{eq_2}};  // NOT_Gate not_6, 4 bits wide
  assign AND_68 = NOT_67 & sum_63;  // AND_Gate and_12, 4 bits wide
  assign AND_69 = {4{eq_2}} & 4'b0000;  // AND_Gate and_13, 4 bits wide
  assign OR_70 = AND_68 | AND_69;  // OR_Gate or_6, 4 bits wide
  Register #(.width(4), .trigger("rising")) CURRENT_abnormal_samples (
    .D(OR_70), .en(sample_enable), .Q(current_counts[25:22]), .clk(clk), .clr(reset));
  Register #(.width(4), .trigger("rising")) COMPLETED_abnormal_samples (
    .D(sum_63), .en(AND_3), .Q(last_completed[25:22]), .clk(clk), .clr(reset));
  Adder #(.width(4)) adder_7 (.a(current_counts[29:26]), .b({3'b000, fault}), .out(sum_73), .cin(1'b0));  // open: cout
  assign NOT_77 = ~{4{eq_2}};  // NOT_Gate not_7, 4 bits wide
  assign AND_78 = NOT_77 & sum_73;  // AND_Gate and_14, 4 bits wide
  assign AND_79 = {4{eq_2}} & 4'b0000;  // AND_Gate and_15, 4 bits wide
  assign OR_80 = AND_78 | AND_79;  // OR_Gate or_7, 4 bits wide
  Register #(.width(4), .trigger("rising")) CURRENT_faults (
    .D(OR_80), .en(sample_enable), .Q(current_counts[29:26]), .clk(clk), .clr(reset));
  Register #(.width(4), .trigger("rising")) COMPLETED_faults (
    .D(sum_73), .en(AND_3), .Q(last_completed[29:26]), .clk(clk), .clr(reset));
  Adder #(.width(4)) adder_8 (.a(window_meta[3:0]), .b(4'b0001), .out(sum_82), .cin(1'b0));  // open: cout
  assign NOT_86 = ~{4{eq_2}};  // NOT_Gate not_8, 4 bits wide
  assign AND_87 = NOT_86 & sum_82;  // AND_Gate and_16, 4 bits wide
  assign AND_88 = {4{eq_2}} & 4'b0000;  // AND_Gate and_17, 4 bits wide
  assign OR_89 = AND_87 | AND_88;  // OR_Gate or_8, 4 bits wide
  Register #(.width(4), .trigger("rising")) POSITION (
    .D(OR_89), .en(sample_enable), .Q(window_meta[3:0]), .clk(clk), .clr(reset));
  Adder #(.width(6)) adder_9 (.a(window_meta[9:4]), .b(6'b000001), .out(sum_91), .cin(1'b0));  // open: cout
  Register #(.width(6), .trigger("rising")) COMPLETED_SEQUENCE (
    .D(sum_91), .en(AND_3), .Q(window_meta[9:4]), .clk(clk), .clr(reset));
  Register #(.width(1), .trigger("rising")) HAS_COMPLETED (
    .D(1'b1), .en(AND_3), .Q(window_meta[10]), .clk(clk), .clr(reset));

  assign current_counts[31:30] = 2'b00;
  assign last_completed[31:30] = 2'b00;
  assign window_meta[31:11] = {21{1'b0}};

  // Other names for the same wires on the sheet: packed_8[3:0] = flags; packed_12[0] = flags[0]; part_4 = flags[0];
  //   packed_22[0] = flags[1]; part_5 = flags[1]; packed_32[0] = flags[2]; part_6 = flags[2]; packed_42[0] = flags[3];
  //   part_7 = flags[3]; packed_52[2:0] = k; packed_62[0] = gt_10; packed_72[0] = fault; packed_16[3:0] = {4{eq_2}};
  //   packed_26[3:0] = {4{eq_2}}; packed_36[3:0] = {4{eq_2}}; packed_46[3:0] = {4{eq_2}}; packed_56[5:0] = {6{eq_2}};
  //   packed_66[3:0] = {4{eq_2}}; packed_76[3:0] = {4{eq_2}}; packed_85[3:0] = {4{eq_2}};
  //   CURRENT_V[3:0] = current_counts[3:0]; packed_95[29:0] = current_counts[29:0];
  //   CURRENT_T[3:0] = current_counts[7:4]; CURRENT_G[3:0] = current_counts[11:8];
  //   CURRENT_A[3:0] = current_counts[15:12]; CURRENT_readings[5:0] = current_counts[21:16];
  //   CURRENT_abnormal_samples[3:0] = current_counts[25:22]; CURRENT_faults[3:0] = current_counts[29:26];
  //   COMPLETED_V[3:0] = last_completed[3:0]; packed_97[29:0] = last_completed[29:0];
  //   COMPLETED_T[3:0] = last_completed[7:4]; COMPLETED_G[3:0] = last_completed[11:8];
  //   COMPLETED_A[3:0] = last_completed[15:12]; COMPLETED_readings[5:0] = last_completed[21:16];
  //   COMPLETED_abnormal_samples[3:0] = last_completed[25:22]; COMPLETED_faults[3:0] = last_completed[29:26];
  //   packed_99[10:0] = window_meta[10:0]; POSITION[3:0] = window_meta[3:0];
  //   COMPLETED_SEQUENCE[5:0] = window_meta[9:4]; HAS_COMPLETED = window_meta[10]
endmodule

module MonitorAux (
  input  [7:0] V,
  input  [7:0] T,
  input  [7:0] G,
  input  [7:0] A,
  input  [3:0] mask,
  input  bV,
  input  bT,
  input  bG,
  input  bA,
  input  eV,
  input  eT,
  input  eG,
  input  eA,
  input  [2:0] k,
  input  watch,
  input  danger,
  input  clk,
  input  reset,
  input  sample_enable,
  output valid,
  output [31:0] status,
  output [31:0] current_counts,
  output [31:0] last_completed,
  output [31:0] window_meta,
  output V_fault,
  output T_fault,
  output G_fault,
  output A_fault
);

  wire eq_24, eq_26, NOT_15, NOT_17, NOT_19, NOT_21;

  Comparator #(.width(8), .mode("unsigned")) comparator_1 (.a(V), .b(8'h64), .gt(status[20]));  // open: eq, lt
  Comparator #(.width(8), .mode("unsigned")) comparator_2 (.a(T), .b(8'h64), .gt(status[21]));  // open: eq, lt
  Comparator #(.width(8), .mode("unsigned")) comparator_3 (.a(G), .b(8'h64), .gt(status[22]));  // open: eq, lt
  Comparator #(.width(8), .mode("unsigned")) comparator_4 (.a(A), .b(8'h64), .gt(status[23]));  // open: eq, lt
  not not_1 (NOT_15, mask[0]);
  or or_1 (V_fault, status[20], NOT_15);
  not not_2 (NOT_17, mask[1]);
  or or_2 (T_fault, status[21], NOT_17);
  not not_3 (NOT_19, mask[2]);
  or or_3 (G_fault, status[22], NOT_19);
  not not_4 (NOT_21, mask[3]);
  or or_4 (A_fault, status[23], NOT_21);
  Comparator #(.width(4), .mode("unsigned")) comparator_5 (.a(status[23:20]), .b(4'b0000), .eq(eq_24));  // open: gt, lt
  Comparator #(.width(4), .mode("unsigned")) comparator_6 (.a(mask), .b(4'b1111), .eq(eq_26));  // open: gt, lt
  and and_1 (status[4], eq_24, eq_26);
  not not_5 (status[15], status[4]);
  or or_5 (status[12], watch, status[15]);
  or or_6 (status[13], danger, status[15]);
  WindowCounters WINDOW_BANK (
    .clk(clk), .reset(reset), .sample_enable(sample_enable), .flags({eA, eG, eT, eV}), .k(k),
    .fault(status[15]), .current_counts(current_counts), .last_completed(last_completed),
    .window_meta(window_meta));

  assign {status[31:24], status[19:16], status[14], status[11:5], status[3:0]} = {{8{1'b0}}, bA, bG, bT, bV, danger, k, eA, eG, eT, eV, mask};
  assign valid = status[4];

  // Other names for the same wires on the sheet: OR_16 = V_fault; OR_18 = T_fault; OR_20 = G_fault; OR_22 = A_fault;
  //   packed_14[3:0] = mask;
  //   packed_35[23:0] = {status[23:20], bA, bG, bT, bV, status[15], danger, status[13:12], k, eA, eG, eT, eV, status[4], mask};
  //   part_10 = mask[0]; part_11 = mask[1]; part_12 = mask[2]; part_13 = mask[3]; AND_27 = status[4];
  //   packed_29[3:0] = {eA, eG, eT, eV}; OR_30 = status[12]; packed_32[1:0] = status[13:12]; OR_31 = status[13];
  //   NOT_28 = status[15]; packed_33[3:0] = {bA, bG, bT, bV}; gt_2 = status[20]; packed_9[3:0] = status[23:20];
  //   gt_4 = status[21]; gt_6 = status[22]; gt_8 = status[23]; WINDOW_BANK_current_counts_36[31:0] = current_counts;
  //   WINDOW_BANK_last_completed_37[31:0] = last_completed; WINDOW_BANK_window_meta_38[31:0] = window_meta
endmodule

module MonitorGUI (
  input  [7:0] V,
  input  [7:0] T,
  input  [7:0] G,
  input  [7:0] A,
  input  [3:0] mask,
  input  clk,
  input  reset,
  input  sample_enable,
  output [31:0] status,
  output [31:0] current_counts,
  output [31:0] last_completed,
  output [31:0] window_meta
);

  wire and_1_out, and_2_out, and_3_out, and_4_out, and_5_out, and_6_out, and_7_out, bA, bG, bT, bV,
       comparator_1_gt, comparator_2_gt, comparator_3_gt, comparator_4_gt, comparator_5_eq, comparator_6_eq,
       comparator_7_gt, DANGER, eA, eG, eT, eV, not_1_out, undriven, undriven_2, undriven_3, undriven_4,
       VALID, Validity__counters_and_protocol_packing_a_fault,
       Validity__counters_and_protocol_packing_g_fault, Validity__counters_and_protocol_packing_t_fault,
       Validity__counters_and_protocol_packing_v_fault, WATCH;
  wire [2:0] adder_1_out, adder_2_out, adder_3_out, bit_extender_1_out, bit_extender_2_out,
       bit_extender_3_out, bit_extender_4_out, K;
  wire [7:0] A_t, G_t, T_t, V_t;

  Comparator #(.width(8), .mode("unsigned")) comparator_1 (.a(V), .b(8'h46), .gt(comparator_1_gt));  // open: eq, lt
  Comparator #(.width(8), .mode("unsigned")) comparator_2 (.a(T), .b(8'h3c), .gt(comparator_2_gt));  // open: eq, lt
  Comparator #(.width(8), .mode("unsigned")) comparator_3 (.a(G), .b(8'h41), .gt(comparator_3_gt));  // open: eq, lt
  Comparator #(.width(8), .mode("unsigned")) comparator_4 (.a(A), .b(8'h46), .gt(comparator_4_gt));  // open: eq, lt
  and and_1 (and_1_out, comparator_1_gt, VALID);
  and and_2 (and_2_out, comparator_2_gt, VALID);
  and and_3 (and_3_out, comparator_3_gt, VALID);
  and and_4 (and_4_out, comparator_4_gt, VALID);
  not not_1 (not_1_out, VALID);
  LED led_1 (.in(undriven));
  LED led_2 (.in(undriven_2));
  LED led_3 (.in(undriven_3));
  LED led_4 (.in(undriven_4));
  LED led_5 (.in(not_1_out));
  assign bit_extender_1_out = {{2{1'b0}}, and_1_out};  // Bit_Extender bit_extender_1
  assign bit_extender_2_out = {{2{1'b0}}, and_2_out};  // Bit_Extender bit_extender_2
  assign bit_extender_3_out = {{2{1'b0}}, and_3_out};  // Bit_Extender bit_extender_3
  assign bit_extender_4_out = {{2{1'b0}}, and_4_out};  // Bit_Extender bit_extender_4
  Adder #(.width(3)) adder_1 (
    .a(bit_extender_1_out), .b(bit_extender_2_out), .out(adder_1_out), .cin(1'b0));  // open: cout
  Adder #(.width(3)) adder_2 (
    .a(bit_extender_3_out), .b(bit_extender_4_out), .out(adder_2_out), .cin(1'b0));  // open: cout
  Adder #(.width(3)) adder_3 (.a(adder_1_out), .b(adder_2_out), .out(adder_3_out), .cin(1'b0));  // open: cout
  MonitorAux Validity__counters_and_protocol_packing (
    .V(V_t), .T(T_t), .G(G_t), .A(A_t), .mask(mask), .bV(bV), .bT(bT), .bG(bG), .bA(bA), .eV(eV), .eT(eT),
    .eG(eG), .eA(eA), .k(K), .watch(WATCH), .danger(DANGER), .clk(clk), .reset(reset),
    .sample_enable(sample_enable), .valid(VALID), .status(status), .current_counts(current_counts),
    .last_completed(last_completed), .window_meta(window_meta),
    .V_fault(Validity__counters_and_protocol_packing_v_fault),
    .T_fault(Validity__counters_and_protocol_packing_t_fault),
    .G_fault(Validity__counters_and_protocol_packing_g_fault),
    .A_fault(Validity__counters_and_protocol_packing_a_fault));
  Comparator #(.width(3), .mode("unsigned")) comparator_5 (
    .a(adder_3_out), .b(3'b000), .eq(comparator_5_eq));  // open: gt, lt
  Comparator #(.width(3), .mode("unsigned")) comparator_6 (
    .a(adder_3_out), .b(3'b001), .eq(comparator_6_eq));  // open: gt, lt
  Comparator #(.width(3), .mode("unsigned")) comparator_7 (
    .a(adder_3_out), .b(3'b001), .gt(comparator_7_gt));  // open: eq, lt
  and and_5 (and_5_out, comparator_5_eq, VALID);
  and and_6 (and_6_out, comparator_6_eq, VALID);
  and and_7 (and_7_out, comparator_7_gt, VALID);
  LED led_6 (.in(Validity__counters_and_protocol_packing_v_fault));
  LED led_7 (.in(Validity__counters_and_protocol_packing_t_fault));
  LED led_8 (.in(Validity__counters_and_protocol_packing_g_fault));
  LED led_9 (.in(Validity__counters_and_protocol_packing_a_fault));
  LED led_10 (.in(and_5_out));
  LED led_11 (.in(and_6_out));
  LED led_12 (.in(and_7_out));

  // Other names for the same wires on the sheet: CUR[31:0] = current_counts; LAST[31:0] = last_completed;
  //   META[31:0] = window_meta

  // Notes on the sheet:
  //   V: initial=0x14
  //   T: initial=0x14
  //   G: initial=0x14
  //   A: initial=0x14
  //   mask: initial=0xf
  //   sample_enable: initial=0x1
  //   VOLCANO MONITOR - numeric thresholds followed by the website digital warning circuit
  //   Unsigned sensor values 0..100. Strict > comparison: equality leaves the digital input OFF.
  //   Manual setup: mask=15 connects all sensors; sample_enable=1 enables clocked sampling.
  //   NORMAL: K=0   WATCH: K=1   DANGER / emergency: K>=2. Invalid rows force eV,eT,eG,eA to 0.
  //   Sampling controls and validity/counter interface (same 10-sample window policy as the website)
  //   Set mask=15 for all four sensors connected.
  //   Pulse reset, then clk with sample_enable=1 to commit a reading.
  //   Instrument outputs for verification: B2 status, B3 current counters, B4 completed counters, B5 window metadata
  //   Threshold 70
  //   Threshold 60
  //   Threshold 65
  //   Threshold 70
  //   V > 70 -> bV
  //   T > 60 -> bT
  //   G > 65 -> bG
  //   A > 70 -> bA
  //   0 ext 1 -> 3
  //   V flag
  //   0 ext 1 -> 3
  //   T flag
  //   0 ext 1 -> 3
  //   G flag
  //   0 ext 1 -> 3
  //   A flag
  //   FAULT = NOT VALID
  //   V + T
  //   G + A
  //   K = eV + eT + eG + eA
  //   K = 0
  //   K = 1
  //   K > 1
  //   Sensor faults
  //   V fault
  //   T fault
  //   G fault
  //   A fault
  //   NORMAL
  //   WATCH
  //   DANGER / EMERGENCY
endmodule
