// Logisim project volcano.circ as structural Verilog: 10 circuits, main circuit MonitorGUI
module ToolchainSmoke (
  output smoke_ok,
  output halt
);


  assign halt = 1'b1;
  assign smoke_ok = 1'b1;
endmodule

module RuleConstants (
  output [7:0] threshold_V,
  output [7:0] threshold_T,
  output [7:0] threshold_G,
  output [7:0] threshold_A
);


  assign threshold_A = 8'h46;
  assign threshold_G = 8'h41;
  assign threshold_T = 8'h3c;
  assign threshold_V = 8'h46;
endmodule

module WindowCounters (
  input  clk,
  input  reset,
  input  sample_enable,
  input  [3:0] flags,
  input  [2:0] k,
  input  fault,
  output [31:0] current_counts,
  output [31:0] last_completed,
  output [31:0] window_meta
);

  wire AND_3, eq_2, gt_10;
  wire [3:0] AND_18, AND_19, AND_28, AND_29, AND_38, AND_39, AND_48, AND_49, AND_68, AND_69, AND_78, AND_79,
       AND_87, AND_88, NOT_17, NOT_27, NOT_37, NOT_47, NOT_67, NOT_77, NOT_86, OR_20, OR_30, OR_40, OR_50,
       OR_70, OR_80, OR_89, sum_13, sum_23, sum_33, sum_43, sum_63, sum_73, sum_82;
  wire [5:0] AND_58, AND_59, NOT_57, OR_60, sum_53, sum_91;

  Comparator #(.width(4), .mode("unsigned")) comparator_1 (
    .a(window_meta[3:0]), .b(4'b1001), .eq(eq_2));  // open: gt, lt
  and and_1 (AND_3, eq_2, sample_enable);
  Comparator #(.width(3), .mode("unsigned")) comparator_2 (.a(k), .b(3'b000), .gt(gt_10));  // open: eq, lt
  Adder #(.width(4)) adder_1 (.a(current_counts[3:0]), .b({3'b000, flags[0]}), .out(sum_13), .cin(1'b0));  // open: cout
  assign NOT_17 = ~{4{eq_2}};  // NOT_Gate not_1, 4 bits wide
  assign AND_18 = NOT_17 & sum_13;  // AND_Gate and_2, 4 bits wide
  assign AND_19 = {4{eq_2}} & 4'b0000;  // AND_Gate and_3, 4 bits wide
  assign OR_20 = AND_18 | AND_19;  // OR_Gate or_1, 4 bits wide
  Register #(.width(4), .trigger("rising")) CURRENT_V (
    .D(OR_20), .en(sample_enable), .Q(current_counts[3:0]), .clk(clk), .clr(reset));
  Register #(.width(4), .trigger("rising")) COMPLETED_V (
    .D(sum_13), .en(AND_3), .Q(last_completed[3:0]), .clk(clk), .clr(reset));
  Adder #(.width(4)) adder_2 (.a(current_counts[7:4]), .b({3'b000, flags[1]}), .out(sum_23), .cin(1'b0));  // open: cout
  assign NOT_27 = ~{4{eq_2}};  // NOT_Gate not_2, 4 bits wide
  assign AND_28 = NOT_27 & sum_23;  // AND_Gate and_4, 4 bits wide
  assign AND_29 = {4{eq_2}} & 4'b0000;  // AND_Gate and_5, 4 bits wide
  assign OR_30 = AND_28 | AND_29;  // OR_Gate or_2, 4 bits wide
  Register #(.width(4), .trigger("rising")) CURRENT_T (
    .D(OR_30), .en(sample_enable), .Q(current_counts[7:4]), .clk(clk), .clr(reset));
  Register #(.width(4), .trigger("rising")) COMPLETED_T (
    .D(sum_23), .en(AND_3), .Q(last_completed[7:4]), .clk(clk), .clr(reset));
  Adder #(.width(4)) adder_3 (
    .a(current_counts[11:8]), .b({3'b000, flags[2]}), .out(sum_33), .cin(1'b0));  // open: cout
  assign NOT_37 = ~{4{eq_2}};  // NOT_Gate not_3, 4 bits wide
  assign AND_38 = NOT_37 & sum_33;  // AND_Gate and_6, 4 bits wide
  assign AND_39 = {4{eq_2}} & 4'b0000;  // AND_Gate and_7, 4 bits wide
  assign OR_40 = AND_38 | AND_39;  // OR_Gate or_3, 4 bits wide
  Register #(.width(4), .trigger("rising")) CURRENT_G (
    .D(OR_40), .en(sample_enable), .Q(current_counts[11:8]), .clk(clk), .clr(reset));
  Register #(.width(4), .trigger("rising")) COMPLETED_G (
    .D(sum_33), .en(AND_3), .Q(last_completed[11:8]), .clk(clk), .clr(reset));
  Adder #(.width(4)) adder_4 (
    .a(current_counts[15:12]), .b({3'b000, flags[3]}), .out(sum_43), .cin(1'b0));  // open: cout
  assign NOT_47 = ~{4{eq_2}};  // NOT_Gate not_4, 4 bits wide
  assign AND_48 = NOT_47 & sum_43;  // AND_Gate and_8, 4 bits wide
  assign AND_49 = {4{eq_2}} & 4'b0000;  // AND_Gate and_9, 4 bits wide
  assign OR_50 = AND_48 | AND_49;  // OR_Gate or_4, 4 bits wide
  Register #(.width(4), .trigger("rising")) CURRENT_A (
    .D(OR_50), .en(sample_enable), .Q(current_counts[15:12]), .clk(clk), .clr(reset));
  Register #(.width(4), .trigger("rising")) COMPLETED_A (
    .D(sum_43), .en(AND_3), .Q(last_completed[15:12]), .clk(clk), .clr(reset));
  Adder #(.width(6)) adder_5 (.a(current_counts[21:16]), .b({3'b000, k}), .out(sum_53), .cin(1'b0));  // open: cout
  assign NOT_57 = ~{6{eq_2}};  // NOT_Gate not_5, 6 bits wide
  assign AND_58 = NOT_57 & sum_53;  // AND_Gate and_10, 6 bits wide
  assign AND_59 = {6{eq_2}} & {6{1'b0}};  // AND_Gate and_11, 6 bits wide
  assign OR_60 = AND_58 | AND_59;  // OR_Gate or_5, 6 bits wide
  Register #(.width(6), .trigger("rising")) CURRENT_readings (
    .D(OR_60), .en(sample_enable), .Q(current_counts[21:16]), .clk(clk), .clr(reset));
  Register #(.width(6), .trigger("rising")) COMPLETED_readings (
    .D(sum_53), .en(AND_3), .Q(last_completed[21:16]), .clk(clk), .clr(reset));
  Adder #(.width(4)) adder_6 (.a(current_counts[25:22]), .b({3'b000, gt_10}), .out(sum_63), .cin(1'b0));  // open: cout
  assign NOT_67 = ~{4{eq_2}};  // NOT_Gate not_6, 4 bits wide
  assign AND_68 = NOT_67 & sum_63;  // AND_Gate and_12, 4 bits wide
  assign AND_69 = {4{eq_2}} & 4'b0000;  // AND_Gate and_13, 4 bits wide
  assign OR_70 = AND_68 | AND_69;  // OR_Gate or_6, 4 bits wide
  Register #(.width(4), .trigger("rising")) CURRENT_abnormal_samples (
    .D(OR_70), .en(sample_enable), .Q(current_counts[25:22]), .clk(clk), .clr(reset));
  Register #(.width(4), .trigger("rising")) COMPLETED_abnormal_samples (
    .D(sum_63), .en(AND_3), .Q(last_completed[25:22]), .clk(clk), .clr(reset));
  Adder #(.width(4)) adder_7 (.a(current_counts[29:26]), .b({3'b000, fault}), .out(sum_73), .cin(1'b0));  // open: cout
  assign NOT_77 = ~{4{eq_2}};  // NOT_Gate not_7, 4 bits wide
  assign AND_78 = NOT_77 & sum_73;  // AND_Gate and_14, 4 bits wide
  assign AND_79 = {4{eq_2}} & 4'b0000;  // AND_Gate and_15, 4 bits wide
  assign OR_80 = AND_78 | AND_79;  // OR_Gate or_7, 4 bits wide
  Register #(.width(4), .trigger("rising")) CURRENT_faults (
    .D(OR_80), .en(sample_enable), .Q(current_counts[29:26]), .clk(clk), .clr(reset));
  Register #(.width(4), .trigger("rising")) COMPLETED_faults (
    .D(sum_73), .en(AND_3), .Q(last_completed[29:26]), .clk(clk), .clr(reset));
  Adder #(.width(4)) adder_8 (.a(window_meta[3:0]), .b(4'b0001), .out(sum_82), .cin(1'b0));  // open: cout
  assign NOT_86 = ~{4{eq_2}};  // NOT_Gate not_8, 4 bits wide
  assign AND_87 = NOT_86 & sum_82;  // AND_Gate and_16, 4 bits wide
  assign AND_88 = {4{eq_2}} & 4'b0000;  // AND_Gate and_17, 4 bits wide
  assign OR_89 = AND_87 | AND_88;  // OR_Gate or_8, 4 bits wide
  Register #(.width(4), .trigger("rising")) POSITION (
    .D(OR_89), .en(sample_enable), .Q(window_meta[3:0]), .clk(clk), .clr(reset));
  Adder #(.width(6)) adder_9 (.a(window_meta[9:4]), .b(6'b000001), .out(sum_91), .cin(1'b0));  // open: cout
  Register #(.width(6), .trigger("rising")) COMPLETED_SEQUENCE (
    .D(sum_91), .en(AND_3), .Q(window_meta[9:4]), .clk(clk), .clr(reset));
  Register #(.width(1), .trigger("rising")) HAS_COMPLETED (
    .D(1'b1), .en(AND_3), .Q(window_meta[10]), .clk(clk), .clr(reset));

  assign current_counts[31:30] = 2'b00;
  assign last_completed[31:30] = 2'b00;
  assign window_meta[31:11] = {21{1'b0}};

  // Other names for the same wires on the sheet: packed_8[3:0] = flags; packed_12[0] = flags[0]; part_4 = flags[0];
  //   packed_22[0] = flags[1]; part_5 = flags[1]; packed_32[0] = flags[2]; part_6 = flags[2]; packed_42[0] = flags[3];
  //   part_7 = flags[3]; packed_52[2:0] = k; packed_62[0] = gt_10; packed_72[0] = fault; packed_16[3:0] = {4{eq_2}};
  //   packed_26[3:0] = {4{eq_2}}; packed_36[3:0] = {4{eq_2}}; packed_46[3:0] = {4{eq_2}}; packed_56[5:0] = {6{eq_2}};
  //   packed_66[3:0] = {4{eq_2}}; packed_76[3:0] = {4{eq_2}}; packed_85[3:0] = {4{eq_2}};
  //   CURRENT_V[3:0] = current_counts[3:0]; packed_95[29:0] = current_counts[29:0];
  //   CURRENT_T[3:0] = current_counts[7:4]; CURRENT_G[3:0] = current_counts[11:8];
  //   CURRENT_A[3:0] = current_counts[15:12]; CURRENT_readings[5:0] = current_counts[21:16];
  //   CURRENT_abnormal_samples[3:0] = current_counts[25:22]; CURRENT_faults[3:0] = current_counts[29:26];
  //   COMPLETED_V[3:0] = last_completed[3:0]; packed_97[29:0] = last_completed[29:0];
  //   COMPLETED_T[3:0] = last_completed[7:4]; COMPLETED_G[3:0] = last_completed[11:8];
  //   COMPLETED_A[3:0] = last_completed[15:12]; COMPLETED_readings[5:0] = last_completed[21:16];
  //   COMPLETED_abnormal_samples[3:0] = last_completed[25:22]; COMPLETED_faults[3:0] = last_completed[29:26];
  //   packed_99[10:0] = window_meta[10:0]; POSITION[3:0] = window_meta[3:0];
  //   COMPLETED_SEQUENCE[5:0] = window_meta[9:4]; HAS_COMPLETED = window_meta[10]
endmodule

module SensorCheck (
  input  [7:0] value,
  input  [7:0] threshold,
  input  connected,
  output raw,
  output range_fault,
  output sensor_fault
);

  wire NOT_4;

  Comparator #(.width(8), .mode("unsigned")) comparator_1 (.a(value), .b(threshold), .gt(raw));  // open: eq, lt
  Comparator #(.width(8), .mode("unsigned")) comparator_2 (.a(value), .b(8'h64), .gt(range_fault));  // open: eq, lt
  not not_1 (NOT_4, connected);
  or or_1 (sensor_fault, range_fault, NOT_4);

  // Other names for the same wires on the sheet: gt_1 = raw; gt_3 = range_fault; OR_5 = sensor_fault
endmodule

module Validity (
  input  [3:0] range_mask,
  input  [3:0] mask,
  output valid,
  output fault
);

  wire eq_2, eq_4;

  Comparator #(.width(4), .mode("unsigned")) comparator_1 (.a(range_mask), .b(4'b0000), .eq(eq_2));  // open: gt, lt
  Comparator #(.width(4), .mode("unsigned")) comparator_2 (.a(mask), .b(4'b1111), .eq(eq_4));  // open: gt, lt
  and and_1 (valid, eq_2, eq_4);
  not not_1 (fault, valid);

  // Other names for the same wires on the sheet: AND_5 = valid; NOT_6 = fault
endmodule

module WarningLogic (
  input  [3:0] raw_mask,
  input  valid,
  output [3:0] effective_mask,
  output [2:0] k,
  output [1:0] warning,
  output emergency,
  output normal,
  output watch,
  output danger,
  output fault
);

  wire eq_24, eq_30, gt_27;
  wire [2:0] sum_16, sum_18;

  assign effective_mask = raw_mask & {4{valid}};  // AND_Gate and_1, 4 bits wide
  Adder #(.width(3)) adder_1 (
    .a({2'b00, effective_mask[0]}), .b({2'b00, effective_mask[1]}), .out(sum_16), .cin(1'b0));  // open: cout
  Adder #(.width(3)) adder_2 (
    .a({2'b00, effective_mask[2]}), .b({2'b00, effective_mask[3]}), .out(sum_18), .cin(1'b0));  // open: cout
  Adder #(.width(3)) adder_3 (.a(sum_16), .b(sum_18), .out(k), .cin(1'b0));  // open: cout
  not not_1 (fault, valid);
  Comparator #(.width(3), .mode("unsigned")) comparator_1 (.a(k), .b(3'b001), .eq(eq_24));  // open: gt, lt
  and and_2 (watch, valid, eq_24);
  Comparator #(.width(3), .mode("unsigned")) comparator_2 (.a(k), .b(3'b001), .gt(gt_27));  // open: eq, lt
  and and_3 (danger, valid, gt_27);
  Comparator #(.width(3), .mode("unsigned")) comparator_3 (.a(k), .b(3'b000), .eq(eq_30));  // open: gt, lt
  and and_4 (normal, valid, eq_30);
  or or_1 (warning[0], watch, fault);
  or or_2 (warning[1], danger, fault);

  assign emergency = danger;

  // Other names for the same wires on the sheet: AND_25 = watch; AND_28 = danger; AND_31 = normal; NOT_22 = fault;
  //   packed_1[3:0] = {4{valid}}; AND_2[3:0] = effective_mask; packed_7[3:0] = effective_mask;
  //   packed_9[0] = effective_mask[0]; part_3 = effective_mask[0]; packed_11[0] = effective_mask[1];
  //   part_4 = effective_mask[1]; packed_13[0] = effective_mask[2]; part_5 = effective_mask[2];
  //   packed_15[0] = effective_mask[3]; part_6 = effective_mask[3]; OR_32 = warning[0]; packed_34[1:0] = warning;
  //   OR_33 = warning[1]; sum_20[2:0] = k
endmodule

module MonitorCore (
  input  [7:0] V,
  input  [7:0] T,
  input  [7:0] G,
  input  [7:0] A,
  input  [3:0] mask,
  input  clk,
  input  reset,
  input  sample_enable,
  output [31:0] status,
  output [3:0] raw_mask,
  output [3:0] range_mask,
  output [3:0] sensor_fault_mask,
  output valid,
  output [3:0] effective_mask,
  output [2:0] k,
  output [1:0] warning,
  output emergency,
  output normal,
  output watch,
  output danger,
  output fault,
  output [31:0] current_counts,
  output [31:0] last_completed,
  output [31:0] window_meta
);

  wire [7:0] THRESHOLDS_threshold_A_4, THRESHOLDS_threshold_G_3, THRESHOLDS_threshold_T_2,
       THRESHOLDS_threshold_V_1;

  RuleConstants THRESHOLDS (
    .threshold_V(THRESHOLDS_threshold_V_1), .threshold_T(THRESHOLDS_threshold_T_2),
    .threshold_G(THRESHOLDS_threshold_G_3), .threshold_A(THRESHOLDS_threshold_A_4));
  SensorCheck SENSOR_V (
    .value(V), .threshold(THRESHOLDS_threshold_V_1), .connected(mask[0]), .raw(raw_mask[0]),
    .range_fault(range_mask[0]), .sensor_fault(sensor_fault_mask[0]));
  SensorCheck SENSOR_T (
    .value(T), .threshold(THRESHOLDS_threshold_T_2), .connected(mask[1]), .raw(raw_mask[1]),
    .range_fault(range_mask[1]), .sensor_fault(sensor_fault_mask[1]));
  SensorCheck SENSOR_G (
    .value(G), .threshold(THRESHOLDS_threshold_G_3), .connected(mask[2]), .raw(raw_mask[2]),
    .range_fault(range_mask[2]), .sensor_fault(sensor_fault_mask[2]));
  SensorCheck SENSOR_A (
    .value(A), .threshold(THRESHOLDS_threshold_A_4), .connected(mask[3]), .raw(raw_mask[3]),
    .range_fault(range_mask[3]), .sensor_fault(sensor_fault_mask[3]));
  Validity CHECK_VALIDITY (.range_mask(range_mask), .mask(mask), .valid(status[4]), .fault(status[15]));
  WarningLogic u_WARNING (
    .raw_mask(raw_mask), .valid(status[4]), .effective_mask(effective_mask), .k(k), .warning(status[13:12]),
    .emergency(emergency), .normal(normal), .watch(watch), .danger(danger), .fault(fault));
  WindowCounters WINDOW_BANK (
    .clk(clk), .reset(reset), .sample_enable(sample_enable), .flags(effective_mask), .k(k),
    .fault(status[15]), .current_counts(current_counts), .last_completed(last_completed),
    .window_meta(window_meta));

  assign {status[31:16], status[14], status[11:5], status[3:0]} = {{8{1'b0}}, range_mask, raw_mask, emergency, k, effective_mask, mask};
  assign valid = status[4];
  assign warning = status[13:12];

  // Other names for the same wires on the sheet: packed_9[3:0] = mask;
  //   packed_35[23:0] = {range_mask, raw_mask, status[15], emergency, status[13:12], k, effective_mask, status[4], mask};
  //   part_5 = mask[0]; part_6 = mask[1]; part_7 = mask[2]; part_8 = mask[3]; CHECK_VALIDITY_valid_24 = status[4];
  //   WARNING_effective_mask_26[3:0] = effective_mask; WARNING_k_27[2:0] = k; WARNING_warning_28[1:0] = status[13:12];
  //   WARNING_emergency_29 = emergency; CHECK_VALIDITY_fault_25 = status[15]; packed_22[3:0] = raw_mask;
  //   SENSOR_V_raw_10 = raw_mask[0]; SENSOR_T_raw_13 = raw_mask[1]; SENSOR_G_raw_16 = raw_mask[2];
  //   SENSOR_A_raw_19 = raw_mask[3]; packed_23[3:0] = range_mask; SENSOR_V_range_fault_11 = range_mask[0];
  //   SENSOR_T_range_fault_14 = range_mask[1]; SENSOR_G_range_fault_17 = range_mask[2];
  //   SENSOR_A_range_fault_20 = range_mask[3]; packed_36[3:0] = sensor_fault_mask;
  //   SENSOR_V_sensor_fault_12 = sensor_fault_mask[0]; SENSOR_T_sensor_fault_15 = sensor_fault_mask[1];
  //   SENSOR_G_sensor_fault_18 = sensor_fault_mask[2]; SENSOR_A_sensor_fault_21 = sensor_fault_mask[3];
  //   WARNING_danger_32 = danger; WARNING_fault_33 = fault; WARNING_normal_30 = normal; WARNING_watch_31 = watch;
  //   WINDOW_BANK_current_counts_37[31:0] = current_counts; WINDOW_BANK_last_completed_38[31:0] = last_completed;
  //   WINDOW_BANK_window_meta_39[31:0] = window_meta
endmodule

module MonitorAux (
  input  [7:0] V,
  input  [7:0] T,
  input  [7:0] G,
  input  [7:0] A,
  input  [3:0] mask,
  input  bV,
  input  bT,
  input  bG,
  input  bA,
  input  eV,
  input  eT,
  input  eG,
  input  eA,
  input  [2:0] k,
  input  watch,
  input  danger,
  input  clk,
  input  reset,
  input  sample_enable,
  output valid,
  output [31:0] status,
  output [31:0] current_counts,
  output [31:0] last_completed,
  output [31:0] window_meta,
  output V_fault,
  output T_fault,
  output G_fault,
  output A_fault
);

  wire eq_24, eq_26, NOT_15, NOT_17, NOT_19, NOT_21;

  Comparator #(.width(8), .mode("unsigned")) comparator_1 (.a(V), .b(8'h64), .gt(status[20]));  // open: eq, lt
  Comparator #(.width(8), .mode("unsigned")) comparator_2 (.a(T), .b(8'h64), .gt(status[21]));  // open: eq, lt
  Comparator #(.width(8), .mode("unsigned")) comparator_3 (.a(G), .b(8'h64), .gt(status[22]));  // open: eq, lt
  Comparator #(.width(8), .mode("unsigned")) comparator_4 (.a(A), .b(8'h64), .gt(status[23]));  // open: eq, lt
  not not_1 (NOT_15, mask[0]);
  or or_1 (V_fault, status[20], NOT_15);
  not not_2 (NOT_17, mask[1]);
  or or_2 (T_fault, status[21], NOT_17);
  not not_3 (NOT_19, mask[2]);
  or or_3 (G_fault, status[22], NOT_19);
  not not_4 (NOT_21, mask[3]);
  or or_4 (A_fault, status[23], NOT_21);
  Comparator #(.width(4), .mode("unsigned")) comparator_5 (.a(status[23:20]), .b(4'b0000), .eq(eq_24));  // open: gt, lt
  Comparator #(.width(4), .mode("unsigned")) comparator_6 (.a(mask), .b(4'b1111), .eq(eq_26));  // open: gt, lt
  and and_1 (status[4], eq_24, eq_26);
  not not_5 (status[15], status[4]);
  or or_5 (status[12], watch, status[15]);
  or or_6 (status[13], danger, status[15]);
  WindowCounters WINDOW_BANK (
    .clk(clk), .reset(reset), .sample_enable(sample_enable), .flags({eA, eG, eT, eV}), .k(k),
    .fault(status[15]), .current_counts(current_counts), .last_completed(last_completed),
    .window_meta(window_meta));

  assign {status[31:24], status[19:16], status[14], status[11:5], status[3:0]} = {{8{1'b0}}, bA, bG, bT, bV, danger, k, eA, eG, eT, eV, mask};
  assign valid = status[4];

  // Other names for the same wires on the sheet: OR_16 = V_fault; OR_18 = T_fault; OR_20 = G_fault; OR_22 = A_fault;
  //   packed_14[3:0] = mask;
  //   packed_35[23:0] = {status[23:20], bA, bG, bT, bV, status[15], danger, status[13:12], k, eA, eG, eT, eV, status[4], mask};
  //   part_10 = mask[0]; part_11 = mask[1]; part_12 = mask[2]; part_13 = mask[3]; AND_27 = status[4];
  //   packed_29[3:0] = {eA, eG, eT, eV}; OR_30 = status[12]; packed_32[1:0] = status[13:12]; OR_31 = status[13];
  //   NOT_28 = status[15]; packed_33[3:0] = {bA, bG, bT, bV}; gt_2 = status[20]; packed_9[3:0] = status[23:20];
  //   gt_4 = status[21]; gt_6 = status[22]; gt_8 = status[23]; WINDOW_BANK_current_counts_36[31:0] = current_counts;
  //   WINDOW_BANK_last_completed_37[31:0] = last_completed; WINDOW_BANK_window_meta_38[31:0] = window_meta
endmodule

module MonitorGUI (
  input  [7:0] V,
  input  [7:0] T,
  input  [7:0] G,
  input  [7:0] A,
  input  [3:0] mask,
  input  clk,
  input  reset,
  input  sample_enable,
  output [31:0] status,
  output [31:0] current_counts,
  output [31:0] last_completed,
  output [31:0] window_meta
);

  wire and_1_out, and_2_out, and_3_out, and_4_out, and_5_out, and_6_out, and_7_out, bA, bG, bT, bV,
       comparator_1_gt, comparator_2_gt, comparator_3_gt, comparator_4_gt, comparator_5_eq, comparator_6_eq,
       comparator_7_gt, DANGER, eA, eG, eT, eV, not_1_out, undriven, undriven_2, undriven_3, undriven_4,
       VALID, Validity__counters_and_protocol_packing_a_fault,
       Validity__counters_and_protocol_packing_g_fault, Validity__counters_and_protocol_packing_t_fault,
       Validity__counters_and_protocol_packing_v_fault, WATCH;
  wire [2:0] adder_1_out, adder_2_out, adder_3_out, bit_extender_1_out, bit_extender_2_out,
       bit_extender_3_out, bit_extender_4_out, K;
  wire [7:0] A_t, G_t, T_t, V_t;

  Comparator #(.width(8), .mode("unsigned")) comparator_1 (.a(V), .b(8'h46), .gt(comparator_1_gt));  // open: eq, lt
  Comparator #(.width(8), .mode("unsigned")) comparator_2 (.a(T), .b(8'h3c), .gt(comparator_2_gt));  // open: eq, lt
  Comparator #(.width(8), .mode("unsigned")) comparator_3 (.a(G), .b(8'h41), .gt(comparator_3_gt));  // open: eq, lt
  Comparator #(.width(8), .mode("unsigned")) comparator_4 (.a(A), .b(8'h46), .gt(comparator_4_gt));  // open: eq, lt
  and and_1 (and_1_out, comparator_1_gt, VALID);
  and and_2 (and_2_out, comparator_2_gt, VALID);
  and and_3 (and_3_out, comparator_3_gt, VALID);
  and and_4 (and_4_out, comparator_4_gt, VALID);
  not not_1 (not_1_out, VALID);
  LED led_1 (.in(undriven));
  LED led_2 (.in(undriven_2));
  LED led_3 (.in(undriven_3));
  LED led_4 (.in(undriven_4));
  LED led_5 (.in(not_1_out));
  assign bit_extender_1_out = {{2{1'b0}}, and_1_out};  // Bit_Extender bit_extender_1
  assign bit_extender_2_out = {{2{1'b0}}, and_2_out};  // Bit_Extender bit_extender_2
  assign bit_extender_3_out = {{2{1'b0}}, and_3_out};  // Bit_Extender bit_extender_3
  assign bit_extender_4_out = {{2{1'b0}}, and_4_out};  // Bit_Extender bit_extender_4
  Adder #(.width(3)) adder_1 (
    .a(bit_extender_1_out), .b(bit_extender_2_out), .out(adder_1_out), .cin(1'b0));  // open: cout
  Adder #(.width(3)) adder_2 (
    .a(bit_extender_3_out), .b(bit_extender_4_out), .out(adder_2_out), .cin(1'b0));  // open: cout
  Adder #(.width(3)) adder_3 (.a(adder_1_out), .b(adder_2_out), .out(adder_3_out), .cin(1'b0));  // open: cout
  MonitorAux Validity__counters_and_protocol_packing (
    .V(V_t), .T(T_t), .G(G_t), .A(A_t), .mask(mask), .bV(bV), .bT(bT), .bG(bG), .bA(bA), .eV(eV), .eT(eT),
    .eG(eG), .eA(eA), .k(K), .watch(WATCH), .danger(DANGER), .clk(clk), .reset(reset),
    .sample_enable(sample_enable), .valid(VALID), .status(status), .current_counts(current_counts),
    .last_completed(last_completed), .window_meta(window_meta),
    .V_fault(Validity__counters_and_protocol_packing_v_fault),
    .T_fault(Validity__counters_and_protocol_packing_t_fault),
    .G_fault(Validity__counters_and_protocol_packing_g_fault),
    .A_fault(Validity__counters_and_protocol_packing_a_fault));
  Comparator #(.width(3), .mode("unsigned")) comparator_5 (
    .a(adder_3_out), .b(3'b000), .eq(comparator_5_eq));  // open: gt, lt
  Comparator #(.width(3), .mode("unsigned")) comparator_6 (
    .a(adder_3_out), .b(3'b001), .eq(comparator_6_eq));  // open: gt, lt
  Comparator #(.width(3), .mode("unsigned")) comparator_7 (
    .a(adder_3_out), .b(3'b001), .gt(comparator_7_gt));  // open: eq, lt
  and and_5 (and_5_out, comparator_5_eq, VALID);
  and and_6 (and_6_out, comparator_6_eq, VALID);
  and and_7 (and_7_out, comparator_7_gt, VALID);
  LED led_6 (.in(Validity__counters_and_protocol_packing_v_fault));
  LED led_7 (.in(Validity__counters_and_protocol_packing_t_fault));
  LED led_8 (.in(Validity__counters_and_protocol_packing_g_fault));
  LED led_9 (.in(Validity__counters_and_protocol_packing_a_fault));
  LED led_10 (.in(and_5_out));
  LED led_11 (.in(and_6_out));
  LED led_12 (.in(and_7_out));

  // Other names for the same wires on the sheet: CUR[31:0] = current_counts; LAST[31:0] = last_completed;
  //   META[31:0] = window_meta

  // Notes on the sheet:
  //   V: initial=0x14
  //   T: initial=0x14
  //   G: initial=0x14
  //   A: initial=0x14
  //   mask: initial=0xf
  //   sample_enable: initial=0x1
  //   VOLCANO MONITOR - numeric thresholds followed by the website digital warning circuit
  //   Unsigned sensor values 0..100. Strict > comparison: equality leaves the digital input OFF.
  //   Manual setup: mask=15 connects all sensors; sample_enable=1 enables clocked sampling.
  //   NORMAL: K=0   WATCH: K=1   DANGER / emergency: K>=2. Invalid rows force eV,eT,eG,eA to 0.
  //   Sampling controls and validity/counter interface (same 10-sample window policy as the website)
  //   Set mask=15 for all four sensors connected.
  //   Pulse reset, then clk with sample_enable=1 to commit a reading.
  //   Instrument outputs for verification: B2 status, B3 current counters, B4 completed counters, B5 window metadata
  //   Threshold 70
  //   Threshold 60
  //   Threshold 65
  //   Threshold 70
  //   V > 70 -> bV
  //   T > 60 -> bT
  //   G > 65 -> bG
  //   A > 70 -> bA
  //   0 ext 1 -> 3
  //   V flag
  //   0 ext 1 -> 3
  //   T flag
  //   0 ext 1 -> 3
  //   G flag
  //   0 ext 1 -> 3
  //   A flag
  //   FAULT = NOT VALID
  //   V + T
  //   G + A
  //   K = eV + eT + eG + eA
  //   K = 0
  //   K = 1
  //   K > 1
  //   Sensor faults
  //   V fault
  //   T fault
  //   G fault
  //   A fault
  //   NORMAL
  //   WATCH
  //   DANGER / EMERGENCY
endmodule

module ReplayHarness (
  output [31:0] B0,
  output [31:0] B1,
  output [31:0] B2,
  output [31:0] B3,
  output [31:0] B4,
  output [31:0] B5,
  output result_valid,
  output [3:0] harness_error,
  output halt
);

  wire AND_215, AND_222, AND_229, AND_239, eq_4, eq_6, eq_8, eq_10, eq_12, eq_14, eq_16, eq_18, eq_20, eq_22,
       eq_24, eq_26, eq_28, eq_32, eq_34, eq_36, eq_41, eq_46, eq_51, eq_53, eq_237, gt_44, MASTER_CLOCK,
       NOT_42, NOT_52, NOT_207, NOT_238, OR_191, OR_192, OR_193, OR_194, OR_195, OR_196, OR_197, OR_198,
       OR_199, OR_200, OR_201, OR_202, OR_203, OR_204, OR_205, OR_206, OR_252, OR_258, OR_264,
       SUBMITTED_MONITOR_danger_290, SUBMITTED_MONITOR_emergency_287, SUBMITTED_MONITOR_fault_291,
       SUBMITTED_MONITOR_normal_288, SUBMITTED_MONITOR_valid_283, SUBMITTED_MONITOR_watch_289;
  wire [1:0] SUBMITTED_MONITOR_warning_286;
  wire [2:0] SUBMITTED_MONITOR_k_285;
  wire [3:0] AND_212, AND_213, AND_219, AND_220, AND_226, AND_227, AND_233, AND_234, NOT_211, NOT_218,
       NOT_225, NOT_232, OR_214, OR_221, OR_228, OR_235, SUBMITTED_MONITOR_effective_mask_284,
       SUBMITTED_MONITOR_range_mask_281, SUBMITTED_MONITOR_raw_mask_280,
       SUBMITTED_MONITOR_sensor_fault_mask_282;
  wire [4:0] AND_75, AND_76, AND_82, AND_83, AND_88, AND_89, AND_95, AND_96, AND_102, AND_103, AND_108,
       AND_109, AND_113, AND_114, AND_118, AND_119, AND_123, AND_124, AND_128, AND_129, AND_133, AND_134,
       AND_138, AND_139, AND_143, AND_144, AND_148, AND_149, AND_153, AND_154, AND_158, AND_159, AND_163,
       AND_164, AND_168, AND_169, AND_173, AND_174, AND_178, AND_179, AND_183, AND_184, AND_188, AND_189,
       CONTROLLER_STATE, NOT_74, NOT_81, NOT_87, NOT_94, NOT_101, NOT_107, NOT_112, NOT_117, NOT_122,
       NOT_127, NOT_132, NOT_137, NOT_142, NOT_147, NOT_152, NOT_157, NOT_162, NOT_167, NOT_172, NOT_177,
       NOT_182, NOT_187, OR_77, OR_84, OR_90, OR_97, OR_104, OR_110, OR_115, OR_120, OR_125, OR_130, OR_135,
       OR_140, OR_145, OR_150, OR_155, OR_160, OR_165, OR_170, OR_175, OR_180, OR_185, OR_190;
  wire [10:0] AND_255, AND_256, AND_261, AND_262, AND_267, AND_268, NOT_254, NOT_260, NOT_266, OR_257,
       OR_263, OR_269, sum_245, sum_248;
  wire [31:0] METADATA_WORD, packed_49, packed_242, packed_275, SAMPLE_COUNT,
       SUBMITTED_MONITOR_current_counts_292, SUBMITTED_MONITOR_last_completed_293,
       SUBMITTED_MONITOR_status_279, SUBMITTED_MONITOR_window_meta_294, sum_38;

  Clock clock_1 (.out(MASTER_CLOCK));
  Comparator #(.width(5), .mode("unsigned")) comparator_1 (
    .a(CONTROLLER_STATE), .b({5{1'b0}}), .eq(eq_4));  // open: gt, lt
  Comparator #(.width(5), .mode("unsigned")) comparator_2 (
    .a(CONTROLLER_STATE), .b(5'b00001), .eq(eq_6));  // open: gt, lt
  Comparator #(.width(5), .mode("unsigned")) comparator_3 (
    .a(CONTROLLER_STATE), .b(5'b00010), .eq(eq_8));  // open: gt, lt
  Comparator #(.width(5), .mode("unsigned")) comparator_4 (
    .a(CONTROLLER_STATE), .b(5'b00011), .eq(eq_10));  // open: gt, lt
  Comparator #(.width(5), .mode("unsigned")) comparator_5 (
    .a(CONTROLLER_STATE), .b(5'b00100), .eq(eq_12));  // open: gt, lt
  Comparator #(.width(5), .mode("unsigned")) comparator_6 (
    .a(CONTROLLER_STATE), .b(5'b00101), .eq(eq_14));  // open: gt, lt
  Comparator #(.width(5), .mode("unsigned")) comparator_7 (
    .a(CONTROLLER_STATE), .b(5'b00110), .eq(eq_16));  // open: gt, lt
  Comparator #(.width(5), .mode("unsigned")) comparator_8 (
    .a(CONTROLLER_STATE), .b(5'b00111), .eq(eq_18));  // open: gt, lt
  Comparator #(.width(5), .mode("unsigned")) comparator_9 (
    .a(CONTROLLER_STATE), .b(5'b01000), .eq(eq_20));  // open: gt, lt
  Comparator #(.width(5), .mode("unsigned")) comparator_10 (
    .a(CONTROLLER_STATE), .b(5'b01001), .eq(eq_22));  // open: gt, lt
  Comparator #(.width(5), .mode("unsigned")) comparator_11 (
    .a(CONTROLLER_STATE), .b(5'b01010), .eq(eq_24));  // open: gt, lt
  Comparator #(.width(5), .mode("unsigned")) comparator_12 (
    .a(CONTROLLER_STATE), .b(5'b01011), .eq(eq_26));  // open: gt, lt
  Comparator #(.width(5), .mode("unsigned")) comparator_13 (
    .a(CONTROLLER_STATE), .b(5'b01100), .eq(eq_28));  // open: gt, lt
  Comparator #(.width(5), .mode("unsigned")) comparator_14 (
    .a(CONTROLLER_STATE), .b(5'b01101), .eq(result_valid));  // open: gt, lt
  Comparator #(.width(5), .mode("unsigned")) comparator_15 (
    .a(CONTROLLER_STATE), .b(5'b01110), .eq(eq_32));  // open: gt, lt
  Comparator #(.width(5), .mode("unsigned")) comparator_16 (
    .a(CONTROLLER_STATE), .b(5'b01111), .eq(eq_34));  // open: gt, lt
  Comparator #(.width(5), .mode("unsigned")) comparator_17 (
    .a(CONTROLLER_STATE), .b(5'b10000), .eq(eq_36));  // open: gt, lt
  Adder #(.width(32)) adder_1 (.a(packed_242), .b(32'h1), .out(sum_38), .cin(1'b0));  // open: cout
  Register #(.width(32), .trigger("rising")) ROW_INDEX (
    .D(sum_38), .en(eq_32), .Q(packed_242), .clk(MASTER_CLOCK), .clr(eq_4));
  Comparator #(.width(32), .mode("unsigned")) comparator_18 (
    .a(packed_49), .b(32'h564d0001), .eq(eq_41));  // open: gt, lt
  not not_1 (NOT_42, eq_41);
  Comparator #(.width(32), .mode("unsigned")) comparator_19 (
    .a(SAMPLE_COUNT), .b(32'h258), .gt(gt_44));  // open: eq, lt
  Comparator #(.width(32), .mode("unsigned")) comparator_20 (
    .a(SAMPLE_COUNT), .b({32{1'b0}}), .eq(eq_46));  // open: gt, lt
  Comparator #(.width(28), .mode("unsigned")) comparator_21 (
    .a(packed_49[31:4]), .b({28{1'b0}}), .eq(eq_51));  // open: gt, lt
  not not_2 (NOT_52, eq_51);
  Comparator #(.width(32), .mode("unsigned")) comparator_22 (.a(sum_38), .b(SAMPLE_COUNT), .eq(eq_53));  // open: gt, lt
  assign NOT_74 = ~{5{NOT_42}};  // NOT_Gate not_3, 5 bits wide
  assign AND_75 = NOT_74 & 5'b00011;  // AND_Gate and_1, 5 bits wide
  assign AND_76 = {5{NOT_42}} & 5'b10000;  // AND_Gate and_2, 5 bits wide
  assign OR_77 = AND_75 | AND_76;  // OR_Gate or_1, 5 bits wide
  assign NOT_81 = ~{5{eq_46}};  // NOT_Gate not_4, 5 bits wide
  assign AND_82 = NOT_81 & 5'b00110;  // AND_Gate and_3, 5 bits wide
  assign AND_83 = {5{eq_46}} & 5'b01111;  // AND_Gate and_4, 5 bits wide
  assign OR_84 = AND_82 | AND_83;  // OR_Gate or_2, 5 bits wide
  assign NOT_87 = ~{5{gt_44}};  // NOT_Gate not_5, 5 bits wide
  assign AND_88 = NOT_87 & OR_84;  // AND_Gate and_5, 5 bits wide
  assign AND_89 = {5{gt_44}} & 5'b10000;  // AND_Gate and_6, 5 bits wide
  assign OR_90 = AND_88 | AND_89;  // OR_Gate or_3, 5 bits wide
  assign NOT_94 = ~{5{NOT_52}};  // NOT_Gate not_6, 5 bits wide
  assign AND_95 = NOT_94 & 5'b01010;  // AND_Gate and_7, 5 bits wide
  assign AND_96 = {5{NOT_52}} & 5'b10000;  // AND_Gate and_8, 5 bits wide
  assign OR_97 = AND_95 | AND_96;  // OR_Gate or_4, 5 bits wide
  assign NOT_101 = ~{5{eq_53}};  // NOT_Gate not_7, 5 bits wide
  assign AND_102 = NOT_101 & 5'b00110;  // AND_Gate and_9, 5 bits wide
  assign AND_103 = {5{eq_53}} & 5'b01111;  // AND_Gate and_10, 5 bits wide
  assign OR_104 = AND_102 | AND_103;  // OR_Gate or_5, 5 bits wide
  assign NOT_107 = ~{5{eq_4}};  // NOT_Gate not_8, 5 bits wide
  assign AND_108 = NOT_107 & 5'b10000;  // AND_Gate and_11, 5 bits wide
  assign AND_109 = {5{eq_4}} & 5'b00001;  // AND_Gate and_12, 5 bits wide
  assign OR_110 = AND_108 | AND_109;  // OR_Gate or_6, 5 bits wide
  assign NOT_112 = ~{5{eq_6}};  // NOT_Gate not_9, 5 bits wide
  assign AND_113 = NOT_112 & OR_110;  // AND_Gate and_13, 5 bits wide
  assign AND_114 = {5{eq_6}} & 5'b00010;  // AND_Gate and_14, 5 bits wide
  assign OR_115 = AND_113 | AND_114;  // OR_Gate or_7, 5 bits wide
  assign NOT_117 = ~{5{eq_8}};  // NOT_Gate not_10, 5 bits wide
  assign AND_118 = NOT_117 & OR_115;  // AND_Gate and_15, 5 bits wide
  assign AND_119 = {5{eq_8}} & OR_77;  // AND_Gate and_16, 5 bits wide
  assign OR_120 = AND_118 | AND_119;  // OR_Gate or_8, 5 bits wide
  assign NOT_122 = ~{5{eq_10}};  // NOT_Gate not_11, 5 bits wide
  assign AND_123 = NOT_122 & OR_120;  // AND_Gate and_17, 5 bits wide
  assign AND_124 = {5{eq_10}} & 5'b00100;  // AND_Gate and_18, 5 bits wide
  assign OR_125 = AND_123 | AND_124;  // OR_Gate or_9, 5 bits wide
  assign NOT_127 = ~{5{eq_12}};  // NOT_Gate not_12, 5 bits wide
  assign AND_128 = NOT_127 & OR_125;  // AND_Gate and_19, 5 bits wide
  assign AND_129 = {5{eq_12}} & 5'b00101;  // AND_Gate and_20, 5 bits wide
  assign OR_130 = AND_128 | AND_129;  // OR_Gate or_10, 5 bits wide
  assign NOT_132 = ~{5{eq_14}};  // NOT_Gate not_13, 5 bits wide
  assign AND_133 = NOT_132 & OR_130;  // AND_Gate and_21, 5 bits wide
  assign AND_134 = {5{eq_14}} & OR_90;  // AND_Gate and_22, 5 bits wide
  assign OR_135 = AND_133 | AND_134;  // OR_Gate or_11, 5 bits wide
  assign NOT_137 = ~{5{eq_16}};  // NOT_Gate not_14, 5 bits wide
  assign AND_138 = NOT_137 & OR_135;  // AND_Gate and_23, 5 bits wide
  assign AND_139 = {5{eq_16}} & 5'b00111;  // AND_Gate and_24, 5 bits wide
  assign OR_140 = AND_138 | AND_139;  // OR_Gate or_12, 5 bits wide
  assign NOT_142 = ~{5{eq_18}};  // NOT_Gate not_15, 5 bits wide
  assign AND_143 = NOT_142 & OR_140;  // AND_Gate and_25, 5 bits wide
  assign AND_144 = {5{eq_18}} & 5'b01000;  // AND_Gate and_26, 5 bits wide
  assign OR_145 = AND_143 | AND_144;  // OR_Gate or_13, 5 bits wide
  assign NOT_147 = ~{5{eq_20}};  // NOT_Gate not_16, 5 bits wide
  assign AND_148 = NOT_147 & OR_145;  // AND_Gate and_27, 5 bits wide
  assign AND_149 = {5{eq_20}} & 5'b01001;  // AND_Gate and_28, 5 bits wide
  assign OR_150 = AND_148 | AND_149;  // OR_Gate or_14, 5 bits wide
  assign NOT_152 = ~{5{eq_22}};  // NOT_Gate not_17, 5 bits wide
  assign AND_153 = NOT_152 & OR_150;  // AND_Gate and_29, 5 bits wide
  assign AND_154 = {5{eq_22}} & OR_97;  // AND_Gate and_30, 5 bits wide
  assign OR_155 = AND_153 | AND_154;  // OR_Gate or_15, 5 bits wide
  assign NOT_157 = ~{5{eq_24}};  // NOT_Gate not_18, 5 bits wide
  assign AND_158 = NOT_157 & OR_155;  // AND_Gate and_31, 5 bits wide
  assign AND_159 = {5{eq_24}} & 5'b01011;  // AND_Gate and_32, 5 bits wide
  assign OR_160 = AND_158 | AND_159;  // OR_Gate or_16, 5 bits wide
  assign NOT_162 = ~{5{eq_26}};  // NOT_Gate not_19, 5 bits wide
  assign AND_163 = NOT_162 & OR_160;  // AND_Gate and_33, 5 bits wide
  assign AND_164 = {5{eq_26}} & 5'b01100;  // AND_Gate and_34, 5 bits wide
  assign OR_165 = AND_163 | AND_164;  // OR_Gate or_17, 5 bits wide
  assign NOT_167 = ~{5{eq_28}};  // NOT_Gate not_20, 5 bits wide
  assign AND_168 = NOT_167 & OR_165;  // AND_Gate and_35, 5 bits wide
  assign AND_169 = {5{eq_28}} & 5'b01101;  // AND_Gate and_36, 5 bits wide
  assign OR_170 = AND_168 | AND_169;  // OR_Gate or_18, 5 bits wide
  assign NOT_172 = ~{5{result_valid}};  // NOT_Gate not_21, 5 bits wide
  assign AND_173 = NOT_172 & OR_170;  // AND_Gate and_37, 5 bits wide
  assign AND_174 = {5{result_valid}} & 5'b01110;  // AND_Gate and_38, 5 bits wide
  assign OR_175 = AND_173 | AND_174;  // OR_Gate or_19, 5 bits wide
  assign NOT_177 = ~{5{eq_32}};  // NOT_Gate not_22, 5 bits wide
  assign AND_178 = NOT_177 & OR_175;  // AND_Gate and_39, 5 bits wide
  assign AND_179 = {5{eq_32}} & OR_104;  // AND_Gate and_40, 5 bits wide
  assign OR_180 = AND_178 | AND_179;  // OR_Gate or_20, 5 bits wide
  assign NOT_182 = ~{5{eq_34}};  // NOT_Gate not_23, 5 bits wide
  assign AND_183 = NOT_182 & OR_180;  // AND_Gate and_41, 5 bits wide
  assign AND_184 = {5{eq_34}} & 5'b01111;  // AND_Gate and_42, 5 bits wide
  assign OR_185 = AND_183 | AND_184;  // OR_Gate or_21, 5 bits wide
  assign NOT_187 = ~{5{eq_36}};  // NOT_Gate not_24, 5 bits wide
  assign AND_188 = NOT_187 & OR_185;  // AND_Gate and_43, 5 bits wide
  assign AND_189 = {5{eq_36}} & 5'b10000;  // AND_Gate and_44, 5 bits wide
  assign OR_190 = AND_188 | AND_189;  // OR_Gate or_22, 5 bits wide
  Register #(.width(5), .trigger("rising")) u_CONTROLLER_STATE (
    .D(OR_190), .en(1'b1), .Q(CONTROLLER_STATE), .clk(MASTER_CLOCK), .clr(1'b0));
  or or_23 (OR_191, eq_4, eq_6);
  or or_24 (OR_192, OR_191, eq_8);
  or or_25 (OR_193, OR_192, eq_10);
  or or_26 (OR_194, OR_193, eq_12);
  or or_27 (OR_195, OR_194, eq_14);
  or or_28 (OR_196, OR_195, eq_16);
  or or_29 (OR_197, OR_196, eq_18);
  or or_30 (OR_198, OR_197, eq_20);
  or or_31 (OR_199, OR_198, eq_22);
  or or_32 (OR_200, OR_199, eq_24);
  or or_33 (OR_201, OR_200, eq_26);
  or or_34 (OR_202, OR_201, eq_28);
  or or_35 (OR_203, OR_202, result_valid);
  or or_36 (OR_204, OR_203, eq_32);
  or or_37 (OR_205, OR_204, eq_34);
  or or_38 (OR_206, OR_205, eq_36);
  not not_25 (NOT_207, OR_206);
  assign NOT_211 = ~{4{NOT_207}};  // NOT_Gate not_26, 4 bits wide
  assign AND_212 = NOT_211 & 4'b0000;  // AND_Gate and_45, 4 bits wide
  assign AND_213 = {4{NOT_207}} & 4'b0100;  // AND_Gate and_46, 4 bits wide
  assign OR_214 = AND_212 | AND_213;  // OR_Gate or_39, 4 bits wide
  and and_47 (AND_215, eq_8, NOT_42);
  assign NOT_218 = ~{4{AND_215}};  // NOT_Gate not_27, 4 bits wide
  assign AND_219 = NOT_218 & OR_214;  // AND_Gate and_48, 4 bits wide
  assign AND_220 = {4{AND_215}} & 4'b0001;  // AND_Gate and_49, 4 bits wide
  assign OR_221 = AND_219 | AND_220;  // OR_Gate or_40, 4 bits wide
  and and_50 (AND_222, eq_14, gt_44);
  assign NOT_225 = ~{4{AND_222}};  // NOT_Gate not_28, 4 bits wide
  assign AND_226 = NOT_225 & OR_221;  // AND_Gate and_51, 4 bits wide
  assign AND_227 = {4{AND_222}} & 4'b0010;  // AND_Gate and_52, 4 bits wide
  assign OR_228 = AND_226 | AND_227;  // OR_Gate or_41, 4 bits wide
  and and_53 (AND_229, eq_22, NOT_52);
  assign NOT_232 = ~{4{AND_229}};  // NOT_Gate not_29, 4 bits wide
  assign AND_233 = NOT_232 & OR_228;  // AND_Gate and_54, 4 bits wide
  assign AND_234 = {4{AND_229}} & 4'b0011;  // AND_Gate and_55, 4 bits wide
  assign OR_235 = AND_233 | AND_234;  // OR_Gate or_42, 4 bits wide
  Comparator #(.width(5), .mode("unsigned")) comparator_23 (.a(OR_190), .b(5'b10000), .eq(eq_237));  // open: gt, lt
  not not_30 (NOT_238, eq_36);
  and and_56 (AND_239, eq_237, NOT_238);
  Register #(.width(4), .trigger("rising")) u_HARNESS_ERROR (
    .D(OR_235), .en(AND_239), .Q(harness_error), .clk(MASTER_CLOCK), .clr(eq_4));
  Adder #(.width(11)) adder_2 (.a({packed_242[9:0], 1'b0}), .b(11'h2), .out(sum_245), .cin(1'b0));  // open: cout
  Adder #(.width(11)) adder_3 (.a(sum_245), .b(11'h1), .out(sum_248), .cin(1'b0));  // open: cout
  or or_43 (OR_252, eq_10, eq_12);
  assign NOT_254 = ~{11{OR_252}};  // NOT_Gate not_31, 11 bits wide
  assign AND_255 = NOT_254 & {11{1'b0}};  // AND_Gate and_57, 11 bits wide
  assign AND_256 = {11{OR_252}} & 11'h1;  // AND_Gate and_58, 11 bits wide
  assign OR_257 = AND_255 | AND_256;  // OR_Gate or_44, 11 bits wide
  or or_45 (OR_258, eq_16, eq_18);
  assign NOT_260 = ~{11{OR_258}};  // NOT_Gate not_32, 11 bits wide
  assign AND_261 = NOT_260 & OR_257;  // AND_Gate and_59, 11 bits wide
  assign AND_262 = {11{OR_258}} & sum_245;  // AND_Gate and_60, 11 bits wide
  assign OR_263 = AND_261 | AND_262;  // OR_Gate or_46, 11 bits wide
  or or_47 (OR_264, eq_20, eq_22);
  assign NOT_266 = ~{11{OR_264}};  // NOT_Gate not_33, 11 bits wide
  assign AND_267 = NOT_266 & OR_263;  // AND_Gate and_61, 11 bits wide
  assign AND_268 = {11{OR_264}} & sum_248;  // AND_Gate and_62, 11 bits wide
  assign OR_269 = AND_267 | AND_268;  // OR_Gate or_48, 11 bits wide
  RAM #(.addrWidth(11), .dataWidth(32), .enables("byte"), .databus("bibus"), .asyncread("true"), .clearpin("false")) STIMULUS_RAM (
    .addr(OR_269), .we(1'b0), .oe(1'b1), .clk(1'b0), .din({32{1'b0}}), .dout(packed_49));
  Register #(.width(32), .trigger("rising")) u_SAMPLE_COUNT (
    .D(packed_49), .en(eq_12), .Q(SAMPLE_COUNT), .clk(MASTER_CLOCK), .clr(eq_4));
  Register #(.width(32), .trigger("rising")) SENSOR_WORD (
    .D(packed_49), .en(eq_18), .Q(packed_275), .clk(MASTER_CLOCK), .clr(eq_4));
  Register #(.width(32), .trigger("rising")) u_METADATA_WORD (
    .D(packed_49), .en(eq_22), .Q(METADATA_WORD), .clk(MASTER_CLOCK), .clr(eq_4));
  MonitorCore SUBMITTED_MONITOR (
    .V(packed_275[7:0]), .T(packed_275[15:8]), .G(packed_275[23:16]), .A(packed_275[31:24]),
    .mask(METADATA_WORD[3:0]), .clk(MASTER_CLOCK), .reset(eq_4), .sample_enable(eq_24),
    .status(SUBMITTED_MONITOR_status_279), .raw_mask(SUBMITTED_MONITOR_raw_mask_280),
    .range_mask(SUBMITTED_MONITOR_range_mask_281),
    .sensor_fault_mask(SUBMITTED_MONITOR_sensor_fault_mask_282), .valid(SUBMITTED_MONITOR_valid_283),
    .effective_mask(SUBMITTED_MONITOR_effective_mask_284), .k(SUBMITTED_MONITOR_k_285),
    .warning(SUBMITTED_MONITOR_warning_286), .emergency(SUBMITTED_MONITOR_emergency_287),
    .normal(SUBMITTED_MONITOR_normal_288), .watch(SUBMITTED_MONITOR_watch_289),
    .danger(SUBMITTED_MONITOR_danger_290), .fault(SUBMITTED_MONITOR_fault_291),
    .current_counts(SUBMITTED_MONITOR_current_counts_292),
    .last_completed(SUBMITTED_MONITOR_last_completed_293), .window_meta(SUBMITTED_MONITOR_window_meta_294));
  Register #(.width(32), .trigger("rising")) SNAPSHOT_B0 (
    .D(packed_242), .en(eq_28), .Q(B0), .clk(MASTER_CLOCK), .clr(eq_4));
  Register #(.width(32), .trigger("rising")) SNAPSHOT_B1 (
    .D(packed_275), .en(eq_28), .Q(B1), .clk(MASTER_CLOCK), .clr(eq_4));
  Register #(.width(32), .trigger("rising")) SNAPSHOT_B2 (
    .D(SUBMITTED_MONITOR_status_279), .en(eq_28), .Q(B2), .clk(MASTER_CLOCK), .clr(eq_4));
  Register #(.width(32), .trigger("rising")) SNAPSHOT_B3 (
    .D(SUBMITTED_MONITOR_current_counts_292), .en(eq_28), .Q(B3), .clk(MASTER_CLOCK), .clr(eq_4));
  Register #(.width(32), .trigger("rising")) SNAPSHOT_B4 (
    .D(SUBMITTED_MONITOR_last_completed_293), .en(eq_28), .Q(B4), .clk(MASTER_CLOCK), .clr(eq_4));
  Register #(.width(32), .trigger("rising")) SNAPSHOT_B5 (
    .D(SUBMITTED_MONITOR_window_meta_294), .en(eq_28), .Q(B5), .clk(MASTER_CLOCK), .clr(eq_4));
  or or_49 (halt, eq_34, eq_36);

  // Other names for the same wires on the sheet: OR_295 = halt; part_47[3:0] = packed_49[3:0];
  //   RAM_WORD[31:0] = packed_49; part_48[27:0] = packed_49[31:4]; packed_73[4:0] = {5{NOT_42}};
  //   packed_80[4:0] = {5{eq_46}}; packed_86[4:0] = {5{gt_44}}; packed_93[4:0] = {5{NOT_52}};
  //   packed_100[4:0] = {5{eq_53}}; packed_106[4:0] = {5{eq_4}}; packed_111[4:0] = {5{eq_6}};
  //   packed_116[4:0] = {5{eq_8}}; packed_121[4:0] = {5{eq_10}}; packed_126[4:0] = {5{eq_12}};
  //   packed_131[4:0] = {5{eq_14}}; packed_136[4:0] = {5{eq_16}}; packed_141[4:0] = {5{eq_18}};
  //   packed_146[4:0] = {5{eq_20}}; packed_151[4:0] = {5{eq_22}}; packed_156[4:0] = {5{eq_24}};
  //   packed_161[4:0] = {5{eq_26}}; packed_166[4:0] = {5{eq_28}}; eq_30 = result_valid;
  //   packed_171[4:0] = {5{result_valid}}; packed_176[4:0] = {5{eq_32}}; packed_181[4:0] = {5{eq_34}};
  //   packed_186[4:0] = {5{eq_36}}; packed_210[3:0] = {4{NOT_207}}; packed_217[3:0] = {4{AND_215}};
  //   packed_224[3:0] = {4{AND_222}}; packed_231[3:0] = {4{AND_229}}; part_241[21:0] = packed_242[31:10];
  //   ROW_INDEX[31:0] = packed_242; packed_243[10:1] = packed_242[9:0]; part_240[9:0] = packed_242[9:0];
  //   packed_253[10:0] = {11{OR_252}}; packed_259[10:0] = {11{OR_258}}; packed_265[10:0] = {11{OR_264}};
  //   part_271[7:0] = packed_275[7:0]; SENSOR_WORD[31:0] = packed_275; part_272[7:0] = packed_275[15:8];
  //   part_273[7:0] = packed_275[23:16]; part_274[7:0] = packed_275[31:24]; packed_278[31:0] = METADATA_WORD;
  //   part_276[3:0] = METADATA_WORD[3:0]; part_277[27:0] = METADATA_WORD[31:4]; SNAPSHOT_B0[31:0] = B0;
  //   SNAPSHOT_B1[31:0] = B1; SNAPSHOT_B2[31:0] = B2; SNAPSHOT_B3[31:0] = B3; SNAPSHOT_B4[31:0] = B4;
  //   SNAPSHOT_B5[31:0] = B5
endmodule
